# Fritzing sketch motor_ldr1 (saved by Fritzing 0.9.3b)
circuit board: 6.88566cm x 5.36311cm
breadboards: 2

parts:
  LED3 = LED - 5mm [color="Green (555nm)" package="5 mm [THT]"]
  R6 = Resistor [tolerance=±5% resistance=10k package=THT]
  R7 = Resistor [tolerance=±5% resistance=330 package=THT]
  Arduino1 = Arduino Uno (Rev3)
  M1 = DC Motor  # not connected
  R10 = Resistor [tolerance=±5% resistance=10k package=THT]
  J1 = screw terminal, 9 pins  # not connected
  S2 = Toggle Switch [package=THT]
  Q1 = Basic FET P-Channel [package="TO220 [THT]"]  # not connected
  D1 = Rectifier Diode [part_number=1N4001 package="300 mil [THT]"]  # not connected
  VCC1 = Battery
  Q2 = PNP-Transistor [package="SOT-23 [SMD]"]  # not connected
  R11 = Resistor [tolerance=±5% resistance=220 package=THT]
  R12 = Resistor [tolerance=±5% resistance=220 package=THT]
  R13 = Resistor [tolerance=±5% resistance=220 package=THT]
  R5 = Photocell (LDR) [package=THT]
  R14 = Photocell (LDR) [package=THT]

nets (from the breadboard view):
  N1: LED3.cathode, R7.Pin_1, Arduino1.D8
  N2: R6.Pin_0, Arduino1.D2, R5.pin_1
  N3: R6.Pin_1, R7.Pin_0, Arduino1.GND, R10.Pin_1
  N4: Arduino1.A0, R10.Pin_0, R14.pin_1
  N5: Arduino1.5V, R5.pin_0, R14.pin_0
  N6: S2.L1, VCC1.+
  N7: S2.COM, VCC1.-
  N8: R11.Pin_0, R12.Pin_1
  N9: R11.Pin_1, R13.Pin_0

notes:
  Controlo de Motor em malha aberta através de LDR
  Ligações ao Arduino UNO
  Circuito de potência do motor
